// Logisim project cpu.circ as structural Verilog: 24 circuits, main circuit main
module main (
  input  [31:0] INSTRUCTION,
  input  CLOCK,
  output [31:0] PROGRAM_COUNTER,
  output [31:0] ra,
  output [31:0] sp,
  output [31:0] t0,
  output [31:0] t1,
  output [31:0] t2,
  output [31:0] s0,
  output [31:0] s1,
  output [31:0] a0
);

  wire ASel, BrEq, BrLT, BrUn, BSel, MemRW, PCSel, RegWEn;
  wire [1:0] LoadSel, WBSel;
  wire [2:0] ImmSel;
  wire [3:0] ALUSel;
  wire [4:0] rd, rs1, rs2;
  wire [31:0] ALUOut, imm, instID, LoadData, MemData, multiplexer_1_out, multiplexer_2_out,
       multiplexer_3_out, PCPlus4, rs1Out, rs2Out, wb;

  Adder #(.width(32)) adder_1 (.a(PROGRAM_COUNTER), .b(32'h4), .out(PCPlus4));  // open: cin, cout
  Register #(.width(32)) register_1 (.D(INSTRUCTION), .clk(CLOCK), .Q(instID));  // open: en, clr
  Multiplexer #(.width(32), .enable("false")) multiplexer_1 (
    .in0(PCPlus4), .in1(ALUOut), .out(multiplexer_1_out), .sel(PCSel));
  Register #(.width(32)) PC (.D(multiplexer_1_out), .clk(CLOCK), .Q(PROGRAM_COUNTER));  // open: en, clr
  ImmRsdDecoder immrsddecoder_1 (
    .Instruction(instID), .rd(rd), .rs1(rs1), .rs2(rs2));  // open: immI, immS, immB, immU, immJ
  ImmGen immgen_1 (.Instruction(instID), .ImmSel(ImmSel), .clk(CLOCK), .imm(imm));
  regfile_main RegFile (
    .rs2(rs2), .rd(rd), .Read_Data_1(rs1Out), .Read_Data_2(rs2Out), .ra(ra), .sp(sp), .t0(t0), .t1(t1),
    .t2(t2), .s0(s0), .s1(s1), .a0(a0), .rs1(rs1), .Write_Data(wb), .RegWEn(RegWEn), .clk(CLOCK));
  BrCmp brcmp_1 (.rs1(rs1Out), .rs2(rs2Out), .BrUn(BrUn), .BrEq(BrEq), .BrLt(BrLT));
  Multiplexer #(.width(32), .enable("false")) multiplexer_2 (
    .in0(rs1Out), .in1(PROGRAM_COUNTER), .out(multiplexer_2_out), .sel(ASel));
  Multiplexer #(.width(32), .enable("false")) multiplexer_3 (
    .in0(rs2Out), .in1(imm), .out(multiplexer_3_out), .sel(BSel));
  Control control_1 (
    .Instruction(INSTRUCTION), .BrEq(BrEq), .BrLt(BrLT), .PCSel(PCSel), .RegWEn(RegWEn), .ImmSel(ImmSel),
    .BrUn(BrUn), .BSel(BSel), .ASel(ASel), .ALUSel(ALUSel), .MemRW(MemRW), .WBSel(WBSel), .LoadSel(LoadSel));
  alu alu_1 (.B(multiplexer_3_out), .Result(ALUOut), .A(multiplexer_2_out), .ALUSel(ALUSel));
  Multiplexer #(.select(2), .width(32), .enable("false")) multiplexer_4 (
    .in0(PCPlus4), .in1(ALUOut), .in2(LoadData), .out(wb), .sel(WBSel));  // open: in3
  // mem_main main_1: pin names not known; wires that end beside it: ALUOut, rs2Out, CLOCK, MemRW, MemData
  LoadExtender loadextender_1 (.MemData(MemData), .LoadSel(LoadSel), .LoadData(LoadData));
  // also tied to GND on the sheet: {ASel, ImmSel[0], ImmSel[1], ImmSel[2], PCSel, WBSel[1]}
  // also tied to VCC on the sheet: {BSel, RegWEn, WBSel[0]}

  // Other names for the same wires on the sheet: clk = CLOCK

  // Notes on the sheet:
  //   Output
  //   IMEM (do **NOT** move this)
  //   Inputs
  //   Inputs/Outputs for testing. Do **NOT** move these.
endmodule

module BrCmp (
  input  [31:0] rs1,
  input  [31:0] rs2,
  input  BrUn,
  output BrEq,
  output BrLt
);

  wire comparator_1_eq, comparator_1_lt, comparator_2_eq, comparator_2_lt;

  Comparator #(.width(32)) comparator_1 (.a(rs1), .b(rs2), .eq(comparator_1_eq), .lt(comparator_1_lt));  // open: gt
  Comparator #(.width(32), .mode("unsigned")) comparator_2 (
    .a(rs1), .b(rs2), .eq(comparator_2_eq), .lt(comparator_2_lt));  // open: gt
  Multiplexer #(.enable("false")) multiplexer_1 (.in0(comparator_1_eq), .in1(comparator_2_eq), .out(BrEq), .sel(BrUn));
  Multiplexer #(.enable("false")) multiplexer_2 (.in0(comparator_1_lt), .in1(comparator_2_lt), .out(BrLt), .sel(BrUn));

  // Other names for the same wires on the sheet: A[31:0] = rs1; B[31:0] = rs2; isUnsigned = BrUn
endmodule

module ImmGen (
  input  [31:0] Instruction,
  input  [2:0] ImmSel,
  input  clk,
  output [31:0] imm
);

  wire [11:0] immI, immS;
  wire [12:0] immB;
  wire [20:0] immJ;
  wire [31:0] B, I, immU, J, S;

  ImmRsdDecoder immrsddecoder_1 (
    .Instruction(Instruction), .immI(immI), .immS(immS), .immB(immB), .immU(immU), .immJ(immJ));  // open: rd, rs1, rs2
  assign I = {{20{immI[11]}}, immI};  // Bit_Extender bit_extender_1
  assign S = {{20{immS[11]}}, immS};  // Bit_Extender bit_extender_2
  assign B = {{19{immB[12]}}, immB};  // Bit_Extender bit_extender_3
  assign J = {{11{immJ[20]}}, immJ};  // Bit_Extender bit_extender_4
  Multiplexer #(.select(3), .width(32), .enable("false")) multiplexer_1 (
    .in0(I), .in1(S), .in2(B), .in3(immU), .in4(J), .out(imm), .sel(ImmSel));  // open: in5, in6, in7

  // Other names for the same wires on the sheet: inst[31:0] = Instruction
endmodule

module LoadExtender (
  input  [31:0] MemData,
  input  [1:0] LoadSel,
  output [31:0] LoadData
);

  wire [31:0] bit_extender_1_out, bit_extender_2_out;

  assign bit_extender_1_out = {{24{MemData[7]}}, MemData[7:0]};  // Bit_Extender bit_extender_1
  assign bit_extender_2_out = {{16{MemData[15]}}, MemData[15:0]};  // Bit_Extender bit_extender_2
  Multiplexer #(.select(2), .width(32), .enable("false")) multiplexer_1 (
    .in0(bit_extender_1_out), .in1(bit_extender_2_out), .in2(MemData), .out(LoadData), .sel(LoadSel));  // open: in3

  // Notes on the sheet:
  //   Currently only supports 0,1,2
  //   LoadSel: 0=lb,1=lh,2=lw,3=lbu,4=lhu
endmodule

module ImmRsdDecoder (
  input  [31:0] Instruction,
  output [4:0] rd,
  output [4:0] rs1,
  output [4:0] rs2,
  output [11:0] immI,
  output [11:0] immS,
  output [12:0] immB,
  output [31:0] immU,
  output [20:0] immJ
);


  assign immB = {Instruction[31], Instruction[7], Instruction[30:25], Instruction[11:8], 1'b0};
  assign immI = Instruction[31:20];
  assign immJ = {Instruction[31], Instruction[19:12], Instruction[20], Instruction[30:21], 1'b0};
  assign immS = {Instruction[31:25], Instruction[11:7]};
  assign immU = {Instruction[31:12], {12{1'b0}}};
  assign rd = Instruction[11:7];
  assign rs1 = Instruction[19:15];
  assign rs2 = Instruction[24:20];

  // Other names for the same wires on the sheet: inst[31:0] = Instruction
endmodule

module OpcodeFunctDecoder (
  input  [31:0] Instruction,
  output Opcode_6,
  output Opcode_5,
  output Opcode_4,
  output Opcode_3,
  output Opcode_2,
  output Opcode_1,
  output Opcode_0,
  output Funct3_2,
  output Funct3_1,
  output Funct3_0,
  output Funct7_6,
  output Funct7_5,
  output Funct7_4,
  output Funct7_3,
  output Funct7_2,
  output Funct7_1,
  output Funct7_0
);


  assign Funct3_0 = Instruction[12];
  assign Funct3_1 = Instruction[13];
  assign Funct3_2 = Instruction[14];
  assign Funct7_0 = Instruction[25];
  assign Funct7_1 = Instruction[26];
  assign Funct7_2 = Instruction[27];
  assign Funct7_3 = Instruction[28];
  assign Funct7_4 = Instruction[29];
  assign Funct7_5 = Instruction[30];
  assign Funct7_6 = Instruction[31];
  assign Opcode_0 = Instruction[0];
  assign Opcode_1 = Instruction[1];
  assign Opcode_2 = Instruction[2];
  assign Opcode_3 = Instruction[3];
  assign Opcode_4 = Instruction[4];
  assign Opcode_5 = Instruction[5];
  assign Opcode_6 = Instruction[6];
endmodule

module Control (
  input  [31:0] Instruction,
  input  BrEq,
  input  BrLt,
  output PCSel,
  output RegWEn,
  output [2:0] ImmSel,
  output BrUn,
  output BSel,
  output ASel,
  output [3:0] ALUSel,
  output MemRW,
  output [1:0] WBSel,
  output [1:0] LoadSel
);

  PCSel_0 pcsel_0_1 (.Instruction(Instruction), .BrEq(BrEq), .BrLt(BrLt), .PCSel(PCSel));
  ALUSel_0 alusel_0_1 (.Instruction(Instruction), .ALUSel_0(ALUSel[0]));
  ALUSel_1 alusel_1_1 (.Instruction(Instruction), .ALUSel_1(ALUSel[1]));
  ALUSel_2 alusel_2_1 (.Instruction(Instruction), .ALUSel_2(ALUSel[2]));
  ALUSel_3 alusel_3_1 (.Instruction(Instruction), .ALUSel_3(ALUSel[3]));
  RegWEn_0 regwen_0_1 (.Instruction(Instruction), .RegWEn(RegWEn));
  ImmSel_0 immsel_0_1 (.Instruction(Instruction), .ImmSel_0(ImmSel[0]));
  ImmSel_1 immsel_1_1 (.Instruction(Instruction), .ImmSel_1(ImmSel[1]));
  ImmSel_2 immsel_2_1 (.Instruction(Instruction), .ImmSel_2(ImmSel[2]));
  BrUn_0 brun_0_1 (.Instruction(Instruction), .BrUn(BrUn));
  ASel_0 asel_0_1 (.Instruction(Instruction), .ASel(ASel));
  BSel_0 bsel_0_1 (.Instruction(Instruction), .BSel(BSel));
  MemRW_0 memrw_0_1 (.Instruction(Instruction), .MemRW(MemRW));
  WBSel_0 wbsel_0_1 (.Instruction(Instruction), .WBSel_0(WBSel[0]));
  WBSel_1 wbsel_1_1 (.Instruction(Instruction), .WBSel_1(WBSel[1]));
  LoadSel_1 loadsel_1_1 (.Instruction(Instruction), .LoadSel_1(LoadSel[0]));
  LoadSel_0 loadsel_0_1 (.Instruction(Instruction), .LoadSel_0(LoadSel[1]));

  // Other names for the same wires on the sheet: inst[31:0] = Instruction
endmodule

module ALUSel_3 (
  input  [31:0] Instruction,
  output ALUSel_3
);

  wire divu, Funct3_0, Funct3_1, Funct3_2, Funct7_0, Funct7_1, Funct7_2, Funct7_3, Funct7_4, Funct7_5,
       Funct7_6, jal, lui, mul, mulh, mulhu, Opcode_0, Opcode_1, Opcode_2, Opcode_3, Opcode_4, Opcode_5,
       Opcode_6, remu, sub;

  OpcodeFunctDecoder opcodefunctdecoder_1 (
    .Instruction(Instruction), .Opcode_6(Opcode_6), .Opcode_5(Opcode_5), .Opcode_4(Opcode_4),
    .Opcode_3(Opcode_3), .Opcode_2(Opcode_2), .Opcode_1(Opcode_1), .Opcode_0(Opcode_0), .Funct3_2(Funct3_2),
    .Funct3_1(Funct3_1), .Funct3_0(Funct3_0), .Funct7_6(Funct7_6), .Funct7_5(Funct7_5), .Funct7_4(Funct7_4),
    .Funct7_3(Funct7_3), .Funct7_2(Funct7_2), .Funct7_1(Funct7_1), .Funct7_0(Funct7_0));
  and and_1 (mul, ~Opcode_6, Opcode_5, Opcode_4, ~Opcode_3, ~Opcode_2, Opcode_1, Opcode_0, ~Funct3_2, ~Funct3_1, ~Funct3_0, ~Funct7_6, ~Funct7_5, ~Funct7_4, ~Funct7_3, ~Funct7_2, ~Funct7_1, Funct7_0);  // AND_Gate
  and and_2 (sub, ~Opcode_6, Opcode_5, Opcode_4, ~Opcode_3, ~Opcode_2, Opcode_1, Opcode_0, ~Funct3_2, ~Funct3_1, ~Funct3_0, ~Funct7_6, Funct7_5, ~Funct7_4, ~Funct7_3, ~Funct7_2, ~Funct7_1, ~Funct7_0);  // AND_Gate
  and and_3 (mulh, ~Opcode_6, Opcode_5, Opcode_4, ~Opcode_3, ~Opcode_2, Opcode_1, Opcode_0, ~Funct3_2, ~Funct3_1, Funct3_0, ~Funct7_6, ~Funct7_5, ~Funct7_4, ~Funct7_3, ~Funct7_2, ~Funct7_1, Funct7_0);  // AND_Gate
  and and_4 (mulhu, ~Opcode_6, Opcode_5, Opcode_4, ~Opcode_3, ~Opcode_2, Opcode_1, Opcode_0, ~Funct3_2, Funct3_1, Funct3_0, ~Funct7_6, ~Funct7_5, ~Funct7_4, ~Funct7_3, ~Funct7_2, ~Funct7_1, Funct7_0);  // AND_Gate
  and and_5 (jal, Opcode_6, Opcode_5, ~Opcode_4, Opcode_3, Opcode_2, Opcode_1, Opcode_0);  // AND_Gate
  and and_6 (lui, ~Opcode_6, Opcode_5, Opcode_4, ~Opcode_3, Opcode_2, Opcode_1, Opcode_0);  // AND_Gate
  and and_7 (remu, ~Opcode_6, Opcode_5, Opcode_4, ~Opcode_3, ~Opcode_2, Opcode_1, Opcode_0, Funct3_2, Funct3_1, Funct3_0, ~Funct7_6, ~Funct7_5, ~Funct7_4, ~Funct7_3, ~Funct7_2, ~Funct7_1, Funct7_0);  // AND_Gate
  and and_8 (divu, ~Opcode_6, Opcode_5, Opcode_4, ~Opcode_3, ~Opcode_2, Opcode_1, Opcode_0, Funct3_2, ~Funct3_1, Funct3_0, ~Funct7_6, ~Funct7_5, ~Funct7_4, ~Funct7_3, ~Funct7_2, ~Funct7_1, Funct7_0);  // AND_Gate
  or or_1 (ALUSel_3, mul, sub, mulh, mulhu, divu, remu, lui, jal);

  // Other names for the same wires on the sheet: inst[31:0] = Instruction
endmodule

module ALUSel_2 (
  input  [31:0] Instruction,
  output ALUSel_2
);

  wire Funct3_0, Funct3_1, Funct3_2, Funct7_0, Funct7_1, Funct7_2, Funct7_3, Funct7_4, Funct7_5, Funct7_6,
       mulh, Opcode_0, Opcode_1, Opcode_2, Opcode_3, Opcode_4, Opcode_5, Opcode_6, sll_0, slt, sra_0, srl_0,
       sub;

  OpcodeFunctDecoder opcodefunctdecoder_1 (
    .Instruction(Instruction), .Opcode_6(Opcode_6), .Opcode_5(Opcode_5), .Opcode_4(Opcode_4),
    .Opcode_3(Opcode_3), .Opcode_2(Opcode_2), .Opcode_1(Opcode_1), .Opcode_0(Opcode_0), .Funct3_2(Funct3_2),
    .Funct3_1(Funct3_1), .Funct3_0(Funct3_0), .Funct7_6(Funct7_6), .Funct7_5(Funct7_5), .Funct7_4(Funct7_4),
    .Funct7_3(Funct7_3), .Funct7_2(Funct7_2), .Funct7_1(Funct7_1), .Funct7_0(Funct7_0));
  and and_1 (sub, ~Opcode_6, Opcode_5, Opcode_4, ~Opcode_3, ~Opcode_2, Opcode_1, Opcode_0, ~Funct3_2, ~Funct3_1, ~Funct3_0, ~Funct7_6, Funct7_5, ~Funct7_4, ~Funct7_3, ~Funct7_2, ~Funct7_1, ~Funct7_0);  // AND_Gate
  and and_2 (mulh, ~Opcode_6, Opcode_5, Opcode_4, ~Opcode_3, ~Opcode_2, Opcode_1, Opcode_0, ~Funct3_2, ~Funct3_1, Funct3_0, ~Funct7_6, ~Funct7_5, ~Funct7_4, ~Funct7_3, ~Funct7_2, ~Funct7_1, Funct7_0);  // AND_Gate
  and and_3 (sll_0, ~Opcode_6, Opcode_5, Opcode_4, ~Opcode_3, ~Opcode_2, Opcode_1, Opcode_0, ~Funct3_2, ~Funct3_1, Funct3_0, ~Funct7_6, ~Funct7_5, ~Funct7_4, ~Funct7_3, ~Funct7_2, ~Funct7_1, ~Funct7_0);  // AND_Gate
  and and_4 (sra_0, ~Opcode_6, Opcode_5, Opcode_4, ~Opcode_3, ~Opcode_2, Opcode_1, Opcode_0, Funct3_2, ~Funct3_1, Funct3_0, ~Funct7_6, Funct7_5, ~Funct7_4, ~Funct7_3, ~Funct7_2, ~Funct7_1, ~Funct7_0);  // AND_Gate
  and and_5 (srl_0, ~Opcode_6, Opcode_5, Opcode_4, ~Opcode_3, ~Opcode_2, Opcode_1, Opcode_0, Funct3_2, ~Funct3_1, Funct3_0, ~Funct7_6, ~Funct7_5, ~Funct7_4, ~Funct7_3, ~Funct7_2, ~Funct7_1, ~Funct7_0);  // AND_Gate
  and and_6 (slt, ~Opcode_6, Opcode_5, Opcode_4, ~Opcode_3, ~Opcode_2, Opcode_1, Opcode_0, ~Funct3_2, Funct3_1, ~Funct3_0, ~Funct7_6, ~Funct7_5, ~Funct7_4, ~Funct7_3, ~Funct7_2, ~Funct7_1, ~Funct7_0);  // AND_Gate
  or or_1 (ALUSel_2, sub, mulh, sll_0, sra_0, srl_0, slt);

  // Other names for the same wires on the sheet: inst[31:0] = Instruction
endmodule

module ALUSel_1 (
  input  [31:0] Instruction,
  output ALUSel_1
);

  wire Funct3_0, Funct3_1, Funct3_2, Funct7_0, Funct7_1, Funct7_2, Funct7_3, Funct7_4, Funct7_5, Funct7_6,
       mul, mulh, mulhu, Opcode_0, Opcode_1, Opcode_2, Opcode_3, Opcode_4, Opcode_5, Opcode_6, or_0, sll_0,
       slt, xor_0;

  OpcodeFunctDecoder opcodefunctdecoder_1 (
    .Instruction(Instruction), .Opcode_6(Opcode_6), .Opcode_5(Opcode_5), .Opcode_4(Opcode_4),
    .Opcode_3(Opcode_3), .Opcode_2(Opcode_2), .Opcode_1(Opcode_1), .Opcode_0(Opcode_0), .Funct3_2(Funct3_2),
    .Funct3_1(Funct3_1), .Funct3_0(Funct3_0), .Funct7_6(Funct7_6), .Funct7_5(Funct7_5), .Funct7_4(Funct7_4),
    .Funct7_3(Funct7_3), .Funct7_2(Funct7_2), .Funct7_1(Funct7_1), .Funct7_0(Funct7_0));
  and and_1 (mul, ~Opcode_6, Opcode_5, Opcode_4, ~Opcode_3, ~Opcode_2, Opcode_1, Opcode_0, ~Funct3_2, ~Funct3_1, ~Funct3_0, ~Funct7_6, ~Funct7_5, ~Funct7_4, ~Funct7_3, ~Funct7_2, ~Funct7_1, Funct7_0);  // AND_Gate
  and and_2 (sll_0, ~Opcode_6, Opcode_5, Opcode_4, ~Opcode_3, ~Opcode_2, Opcode_1, Opcode_0, ~Funct3_2, ~Funct3_1, Funct3_0, ~Funct7_6, ~Funct7_5, ~Funct7_4, ~Funct7_3, ~Funct7_2, ~Funct7_1, ~Funct7_0);  // AND_Gate
  and and_3 (mulh, ~Opcode_6, Opcode_5, Opcode_4, ~Opcode_3, ~Opcode_2, Opcode_1, Opcode_0, ~Funct3_2, ~Funct3_1, Funct3_0, ~Funct7_6, ~Funct7_5, ~Funct7_4, ~Funct7_3, ~Funct7_2, ~Funct7_1, Funct7_0);  // AND_Gate
  and and_4 (slt, ~Opcode_6, Opcode_5, Opcode_4, ~Opcode_3, ~Opcode_2, Opcode_1, Opcode_0, ~Funct3_2, Funct3_1, ~Funct3_0, ~Funct7_6, ~Funct7_5, ~Funct7_4, ~Funct7_3, ~Funct7_2, ~Funct7_1, ~Funct7_0);  // AND_Gate
  and and_5 (mulhu, ~Opcode_6, Opcode_5, Opcode_4, ~Opcode_3, ~Opcode_2, Opcode_1, Opcode_0, ~Funct3_2, Funct3_1, Funct3_0, ~Funct7_6, ~Funct7_5, ~Funct7_4, ~Funct7_3, ~Funct7_2, ~Funct7_1, Funct7_0);  // AND_Gate
  and and_6 (xor_0, ~Opcode_6, Opcode_5, Opcode_4, ~Opcode_3, ~Opcode_2, Opcode_1, Opcode_0, Funct3_2, ~Funct3_1, ~Funct3_0, ~Funct7_6, ~Funct7_5, ~Funct7_4, ~Funct7_3, ~Funct7_2, ~Funct7_1, ~Funct7_0);  // AND_Gate
  and and_7 (or_0, ~Opcode_6, Opcode_5, Opcode_4, ~Opcode_3, ~Opcode_2, Opcode_1, Opcode_0, Funct3_2, Funct3_1, ~Funct3_0, ~Funct7_6, ~Funct7_5, ~Funct7_4, ~Funct7_3, ~Funct7_2, ~Funct7_1, ~Funct7_0);  // AND_Gate

  // Other names for the same wires on the sheet: inst[31:0] = Instruction
endmodule

module ALUSel_0 (
  input  [31:0] Instruction,
  output ALUSel_0
);

  wire Funct3_0, Funct3_1, Funct3_2, Funct7_0, Funct7_1, Funct7_2, Funct7_3, Funct7_4, Funct7_5, Funct7_6,
       Opcode_0, Opcode_1, Opcode_2, Opcode_3, Opcode_4, Opcode_5, Opcode_6;

  OpcodeFunctDecoder opcodefunctdecoder_1 (
    .Instruction(Instruction), .Opcode_6(Opcode_6), .Opcode_5(Opcode_5), .Opcode_4(Opcode_4),
    .Opcode_3(Opcode_3), .Opcode_2(Opcode_2), .Opcode_1(Opcode_1), .Opcode_0(Opcode_0), .Funct3_2(Funct3_2),
    .Funct3_1(Funct3_1), .Funct3_0(Funct3_0), .Funct7_6(Funct7_6), .Funct7_5(Funct7_5), .Funct7_4(Funct7_4),
    .Funct7_3(Funct7_3), .Funct7_2(Funct7_2), .Funct7_1(Funct7_1), .Funct7_0(Funct7_0));

  // Other names for the same wires on the sheet: inst[31:0] = Instruction
endmodule

module RegWEn_0 (
  input  [31:0] Instruction,
  output RegWEn
);

  wire Funct3_0, Funct3_1, Funct3_2, Funct7_0, Funct7_1, Funct7_2, Funct7_3, Funct7_4, Funct7_5, Funct7_6,
       Opcode_0, Opcode_1, Opcode_2, Opcode_3, Opcode_4, Opcode_5, Opcode_6;

  OpcodeFunctDecoder opcodefunctdecoder_1 (
    .Instruction(Instruction), .Opcode_6(Opcode_6), .Opcode_5(Opcode_5), .Opcode_4(Opcode_4),
    .Opcode_3(Opcode_3), .Opcode_2(Opcode_2), .Opcode_1(Opcode_1), .Opcode_0(Opcode_0), .Funct3_2(Funct3_2),
    .Funct3_1(Funct3_1), .Funct3_0(Funct3_0), .Funct7_6(Funct7_6), .Funct7_5(Funct7_5), .Funct7_4(Funct7_4),
    .Funct7_3(Funct7_3), .Funct7_2(Funct7_2), .Funct7_1(Funct7_1), .Funct7_0(Funct7_0));

  // Other names for the same wires on the sheet: inst[31:0] = Instruction
endmodule

module ImmSel_2 (
  input  [31:0] Instruction,
  output ImmSel_2
);

  wire Funct3_0, Funct3_1, Funct3_2, Funct7_0, Funct7_1, Funct7_2, Funct7_3, Funct7_4, Funct7_5, Funct7_6,
       Opcode_0, Opcode_1, Opcode_2, Opcode_3, Opcode_4, Opcode_5, Opcode_6;

  OpcodeFunctDecoder opcodefunctdecoder_1 (
    .Instruction(Instruction), .Opcode_6(Opcode_6), .Opcode_5(Opcode_5), .Opcode_4(Opcode_4),
    .Opcode_3(Opcode_3), .Opcode_2(Opcode_2), .Opcode_1(Opcode_1), .Opcode_0(Opcode_0), .Funct3_2(Funct3_2),
    .Funct3_1(Funct3_1), .Funct3_0(Funct3_0), .Funct7_6(Funct7_6), .Funct7_5(Funct7_5), .Funct7_4(Funct7_4),
    .Funct7_3(Funct7_3), .Funct7_2(Funct7_2), .Funct7_1(Funct7_1), .Funct7_0(Funct7_0));

  // Other names for the same wires on the sheet: inst[31:0] = Instruction
endmodule

module ImmSel_1 (
  input  [31:0] Instruction,
  output ImmSel_1
);

  wire Funct3_0, Funct3_1, Funct3_2, Funct7_0, Funct7_1, Funct7_2, Funct7_3, Funct7_4, Funct7_5, Funct7_6,
       Opcode_0, Opcode_1, Opcode_2, Opcode_3, Opcode_4, Opcode_5, Opcode_6;

  OpcodeFunctDecoder opcodefunctdecoder_1 (
    .Instruction(Instruction), .Opcode_6(Opcode_6), .Opcode_5(Opcode_5), .Opcode_4(Opcode_4),
    .Opcode_3(Opcode_3), .Opcode_2(Opcode_2), .Opcode_1(Opcode_1), .Opcode_0(Opcode_0), .Funct3_2(Funct3_2),
    .Funct3_1(Funct3_1), .Funct3_0(Funct3_0), .Funct7_6(Funct7_6), .Funct7_5(Funct7_5), .Funct7_4(Funct7_4),
    .Funct7_3(Funct7_3), .Funct7_2(Funct7_2), .Funct7_1(Funct7_1), .Funct7_0(Funct7_0));

  // Other names for the same wires on the sheet: inst[31:0] = Instruction
endmodule

module ImmSel_0 (
  input  [31:0] Instruction,
  output ImmSel_0
);

  wire Funct3_0, Funct3_1, Funct3_2, Funct7_0, Funct7_1, Funct7_2, Funct7_3, Funct7_4, Funct7_5, Funct7_6,
       Opcode_0, Opcode_1, Opcode_2, Opcode_3, Opcode_4, Opcode_5, Opcode_6;

  OpcodeFunctDecoder opcodefunctdecoder_1 (
    .Instruction(Instruction), .Opcode_6(Opcode_6), .Opcode_5(Opcode_5), .Opcode_4(Opcode_4),
    .Opcode_3(Opcode_3), .Opcode_2(Opcode_2), .Opcode_1(Opcode_1), .Opcode_0(Opcode_0), .Funct3_2(Funct3_2),
    .Funct3_1(Funct3_1), .Funct3_0(Funct3_0), .Funct7_6(Funct7_6), .Funct7_5(Funct7_5), .Funct7_4(Funct7_4),
    .Funct7_3(Funct7_3), .Funct7_2(Funct7_2), .Funct7_1(Funct7_1), .Funct7_0(Funct7_0));

  // Other names for the same wires on the sheet: inst[31:0] = Instruction
endmodule

module BrUn_0 (
  input  [31:0] Instruction,
  output BrUn
);

  wire Funct3_0, Funct3_1, Funct3_2, Funct7_0, Funct7_1, Funct7_2, Funct7_3, Funct7_4, Funct7_5, Funct7_6,
       Opcode_0, Opcode_1, Opcode_2, Opcode_3, Opcode_4, Opcode_5, Opcode_6;

  OpcodeFunctDecoder opcodefunctdecoder_1 (
    .Instruction(Instruction), .Opcode_6(Opcode_6), .Opcode_5(Opcode_5), .Opcode_4(Opcode_4),
    .Opcode_3(Opcode_3), .Opcode_2(Opcode_2), .Opcode_1(Opcode_1), .Opcode_0(Opcode_0), .Funct3_2(Funct3_2),
    .Funct3_1(Funct3_1), .Funct3_0(Funct3_0), .Funct7_6(Funct7_6), .Funct7_5(Funct7_5), .Funct7_4(Funct7_4),
    .Funct7_3(Funct7_3), .Funct7_2(Funct7_2), .Funct7_1(Funct7_1), .Funct7_0(Funct7_0));

  // Other names for the same wires on the sheet: inst[31:0] = Instruction
endmodule

module ASel_0 (
  input  [31:0] Instruction,
  output ASel
);

  wire Funct3_0, Funct3_1, Funct3_2, Funct7_0, Funct7_1, Funct7_2, Funct7_3, Funct7_4, Funct7_5, Funct7_6,
       Opcode_0, Opcode_1, Opcode_2, Opcode_3, Opcode_4, Opcode_5, Opcode_6;

  OpcodeFunctDecoder opcodefunctdecoder_1 (
    .Instruction(Instruction), .Opcode_6(Opcode_6), .Opcode_5(Opcode_5), .Opcode_4(Opcode_4),
    .Opcode_3(Opcode_3), .Opcode_2(Opcode_2), .Opcode_1(Opcode_1), .Opcode_0(Opcode_0), .Funct3_2(Funct3_2),
    .Funct3_1(Funct3_1), .Funct3_0(Funct3_0), .Funct7_6(Funct7_6), .Funct7_5(Funct7_5), .Funct7_4(Funct7_4),
    .Funct7_3(Funct7_3), .Funct7_2(Funct7_2), .Funct7_1(Funct7_1), .Funct7_0(Funct7_0));

  // Other names for the same wires on the sheet: inst[31:0] = Instruction
endmodule

module BSel_0 (
  input  [31:0] Instruction,
  output BSel
);

  wire Funct3_0, Funct3_1, Funct3_2, Funct7_0, Funct7_1, Funct7_2, Funct7_3, Funct7_4, Funct7_5, Funct7_6,
       Opcode_0, Opcode_1, Opcode_2, Opcode_3, Opcode_4, Opcode_5, Opcode_6;

  OpcodeFunctDecoder opcodefunctdecoder_1 (
    .Instruction(Instruction), .Opcode_6(Opcode_6), .Opcode_5(Opcode_5), .Opcode_4(Opcode_4),
    .Opcode_3(Opcode_3), .Opcode_2(Opcode_2), .Opcode_1(Opcode_1), .Opcode_0(Opcode_0), .Funct3_2(Funct3_2),
    .Funct3_1(Funct3_1), .Funct3_0(Funct3_0), .Funct7_6(Funct7_6), .Funct7_5(Funct7_5), .Funct7_4(Funct7_4),
    .Funct7_3(Funct7_3), .Funct7_2(Funct7_2), .Funct7_1(Funct7_1), .Funct7_0(Funct7_0));

  // Other names for the same wires on the sheet: inst[31:0] = Instruction
endmodule

module MemRW_0 (
  input  [31:0] Instruction,
  output MemRW
);

  wire Funct3_0, Funct3_1, Funct3_2, Funct7_0, Funct7_1, Funct7_2, Funct7_3, Funct7_4, Funct7_5, Funct7_6,
       Opcode_0, Opcode_1, Opcode_2, Opcode_3, Opcode_4, Opcode_5, Opcode_6;

  OpcodeFunctDecoder opcodefunctdecoder_1 (
    .Instruction(Instruction), .Opcode_6(Opcode_6), .Opcode_5(Opcode_5), .Opcode_4(Opcode_4),
    .Opcode_3(Opcode_3), .Opcode_2(Opcode_2), .Opcode_1(Opcode_1), .Opcode_0(Opcode_0), .Funct3_2(Funct3_2),
    .Funct3_1(Funct3_1), .Funct3_0(Funct3_0), .Funct7_6(Funct7_6), .Funct7_5(Funct7_5), .Funct7_4(Funct7_4),
    .Funct7_3(Funct7_3), .Funct7_2(Funct7_2), .Funct7_1(Funct7_1), .Funct7_0(Funct7_0));

  // Other names for the same wires on the sheet: inst[31:0] = Instruction
endmodule

module WBSel_1 (
  input  [31:0] Instruction,
  output WBSel_1
);

  wire Funct3_0, Funct3_1, Funct3_2, Funct7_0, Funct7_1, Funct7_2, Funct7_3, Funct7_4, Funct7_5, Funct7_6,
       Opcode_0, Opcode_1, Opcode_2, Opcode_3, Opcode_4, Opcode_5, Opcode_6;

  OpcodeFunctDecoder opcodefunctdecoder_1 (
    .Instruction(Instruction), .Opcode_6(Opcode_6), .Opcode_5(Opcode_5), .Opcode_4(Opcode_4),
    .Opcode_3(Opcode_3), .Opcode_2(Opcode_2), .Opcode_1(Opcode_1), .Opcode_0(Opcode_0), .Funct3_2(Funct3_2),
    .Funct3_1(Funct3_1), .Funct3_0(Funct3_0), .Funct7_6(Funct7_6), .Funct7_5(Funct7_5), .Funct7_4(Funct7_4),
    .Funct7_3(Funct7_3), .Funct7_2(Funct7_2), .Funct7_1(Funct7_1), .Funct7_0(Funct7_0));

  // Other names for the same wires on the sheet: inst[31:0] = Instruction
endmodule

module WBSel_0 (
  input  [31:0] Instruction,
  output WBSel_0
);

  wire Funct3_0, Funct3_1, Funct3_2, Funct7_0, Funct7_1, Funct7_2, Funct7_3, Funct7_4, Funct7_5, Funct7_6,
       Opcode_0, Opcode_1, Opcode_2, Opcode_3, Opcode_4, Opcode_5, Opcode_6;

  OpcodeFunctDecoder opcodefunctdecoder_1 (
    .Instruction(Instruction), .Opcode_6(Opcode_6), .Opcode_5(Opcode_5), .Opcode_4(Opcode_4),
    .Opcode_3(Opcode_3), .Opcode_2(Opcode_2), .Opcode_1(Opcode_1), .Opcode_0(Opcode_0), .Funct3_2(Funct3_2),
    .Funct3_1(Funct3_1), .Funct3_0(Funct3_0), .Funct7_6(Funct7_6), .Funct7_5(Funct7_5), .Funct7_4(Funct7_4),
    .Funct7_3(Funct7_3), .Funct7_2(Funct7_2), .Funct7_1(Funct7_1), .Funct7_0(Funct7_0));

  // Other names for the same wires on the sheet: inst[31:0] = Instruction
endmodule

module PCSel_0 (
  input  [31:0] Instruction,
  input  BrEq,
  input  BrLt,
  output PCSel
);

  wire Funct3_0, Funct3_1, Funct3_2, Funct7_0, Funct7_1, Funct7_2, Funct7_3, Funct7_4, Funct7_5, Funct7_6,
       Opcode_0, Opcode_1, Opcode_2, Opcode_3, Opcode_4, Opcode_5, Opcode_6;

  OpcodeFunctDecoder opcodefunctdecoder_1 (
    .Instruction(Instruction), .Opcode_6(Opcode_6), .Opcode_5(Opcode_5), .Opcode_4(Opcode_4),
    .Opcode_3(Opcode_3), .Opcode_2(Opcode_2), .Opcode_1(Opcode_1), .Opcode_0(Opcode_0), .Funct3_2(Funct3_2),
    .Funct3_1(Funct3_1), .Funct3_0(Funct3_0), .Funct7_6(Funct7_6), .Funct7_5(Funct7_5), .Funct7_4(Funct7_4),
    .Funct7_3(Funct7_3), .Funct7_2(Funct7_2), .Funct7_1(Funct7_1), .Funct7_0(Funct7_0));

  // Other names for the same wires on the sheet: inst[31:0] = Instruction
endmodule

module LoadSel_1 (
  input  [31:0] Instruction,
  output LoadSel_1
);

  wire Funct3_0, Funct3_1, Funct3_2, Funct7_0, Funct7_1, Funct7_2, Funct7_3, Funct7_4, Funct7_5, Funct7_6,
       Opcode_0, Opcode_1, Opcode_2, Opcode_3, Opcode_4, Opcode_5, Opcode_6;

  OpcodeFunctDecoder opcodefunctdecoder_1 (
    .Instruction(Instruction), .Opcode_6(Opcode_6), .Opcode_5(Opcode_5), .Opcode_4(Opcode_4),
    .Opcode_3(Opcode_3), .Opcode_2(Opcode_2), .Opcode_1(Opcode_1), .Opcode_0(Opcode_0), .Funct3_2(Funct3_2),
    .Funct3_1(Funct3_1), .Funct3_0(Funct3_0), .Funct7_6(Funct7_6), .Funct7_5(Funct7_5), .Funct7_4(Funct7_4),
    .Funct7_3(Funct7_3), .Funct7_2(Funct7_2), .Funct7_1(Funct7_1), .Funct7_0(Funct7_0));

  // Other names for the same wires on the sheet: inst[31:0] = Instruction
endmodule

module LoadSel_0 (
  input  [31:0] Instruction,
  output LoadSel_0
);

  wire Funct3_0, Funct3_1, Funct3_2, Funct7_0, Funct7_1, Funct7_2, Funct7_3, Funct7_4, Funct7_5, Funct7_6,
       Opcode_0, Opcode_1, Opcode_2, Opcode_3, Opcode_4, Opcode_5, Opcode_6;

  OpcodeFunctDecoder opcodefunctdecoder_1 (
    .Instruction(Instruction), .Opcode_6(Opcode_6), .Opcode_5(Opcode_5), .Opcode_4(Opcode_4),
    .Opcode_3(Opcode_3), .Opcode_2(Opcode_2), .Opcode_1(Opcode_1), .Opcode_0(Opcode_0), .Funct3_2(Funct3_2),
    .Funct3_1(Funct3_1), .Funct3_0(Funct3_0), .Funct7_6(Funct7_6), .Funct7_5(Funct7_5), .Funct7_4(Funct7_4),
    .Funct7_3(Funct7_3), .Funct7_2(Funct7_2), .Funct7_1(Funct7_1), .Funct7_0(Funct7_0));

  // Other names for the same wires on the sheet: inst[31:0] = Instruction
endmodule
